# Fritzing sketch FritzingBošnjak (saved by Fritzing 0.9.3b)
breadboards: 1

parts:
  Part1 = Arduino Uno (Rev3)
  R1 = Resistor [tolerance=±5% resistance=220 package="0603 [SMD]"]
  DI1 = 7-Segment LED Display [package=THT]
  HC-SR04_Sensor_1 = HC-SR04 Ultrasonic Distance Sensor

nets:
  N1: Part1.D8, DI1.cathodeG
  N2: Part1.D9_PWM, DI1.cathodeDP
  N3: Part1.D11_PWM/MOSI, HC-SR04_Sensor_1.TRIG
  N4: Part1.D12/MISO, HC-SR04_Sensor_1.ECHO
  N5: Part1.D2, DI1.cathodeB
  N6: Part1.D3_PWM, DI1.cathodeA
  N7: Part1.D4, DI1.cathodeC
  N8: Part1.D5_PWM, DI1.cathodeD
  N9: Part1.D6_PWM, DI1.cathodeE
  N10: Part1.D7, DI1.cathodeF
  5V: Part1.5V, R1.Pin_1, HC-SR04_Sensor_1.VCC
  GND: Part1.GND, HC-SR04_Sensor_1.GND
  N11: R1.Pin_0, DI1.commAnode#2

// code stored in the sketch: FritzingIvanBoÜnjak.ino
int trigPin = 11;
int echoPin = 12;
int A = 2;
int B = 3;
int C = 4;
int D = 5;
int E = 6;
int F = 7;
int G = 8;
int DP = 9;
long duration, cm, inches;


void setup() {
  Serial.begin (9600); 
  pinMode(trigPin, OUTPUT); 
  pinMode(echoPin, INPUT); 
  pinMode(A, OUTPUT); 
  pinMode(B, OUTPUT); 
  pinMode(C, OUTPUT); 
  pinMode(D, OUTPUT); 
  pinMode(E, OUTPUT); 
  pinMode(F, OUTPUT); 
  pinMode(G, OUTPUT); 
  pinMode(DP, OUTPUT); 
}
 
void loop() {
  digitalWrite(trigPin, LOW); 
  delayMicroseconds(5); 
  digitalWrite(trigPin, HIGH); 
  delayMicroseconds(10); 
  digitalWrite(trigPin, LOW); 
  pinMode(echoPin, INPUT); 


  duration = pulseIn(echoPin, HIGH);
  cm = (duration/2)/29.1;
  inches = (duration/2)/74; 


  Serial.print(inches); 
  Serial.print("in, ");
  Serial.print(cm); 
  Serial.print("cm");
  Serial.println();
  delay(250);


  if (cm < 20) {
    digitalWrite(A, LOW);
    digitalWrite(B, LOW);
    digitalWrite(C, LOW);
    digitalWrite(D, LOW);
    digitalWrite(E, LOW);
    digitalWrite(F, LOW);
    digitalWrite(G, LOW);
    digitalWrite(DP, LOW);
  }
  if (cm => 20) {
    digitalWrite(A, HIGH);
    digitalWrite(B, LOW);
    digitalWrite(C, HIGH);
    digitalWrite(D, HIGH);
    digitalWrite(E, HIGH);
    digitalWrite(F, LOW);
    digitalWrite(G, HIGH);
    digitalWrite(DP, HIGH);
  }
  if (cm => 40) {
    digitalWrite(A, HIGH);
    digitalWrite(B, HIGH);
    digitalWrite(C, LOW);
    digitalWrite(D, HIGH);
    digitalWrite(E, LOW);
    digitalWrite(F, HIGH);
    digitalWrite(G, HIGH);
    digitalWrite(DP, HIGH);
  }
  if (cm => 60) {
    digitalWrite(A, HIGH);
    digitalWrite(B, HIGH);
    digitalWrite(C, HIGH);
    digitalWrite(D, HIGH);
    digitalWrite(E, HIGH);
    digitalWrite(F, HIGH);
    digitalWrite(G, LOW);
    digitalWrite(DP, HIGH);
  }
}

// code stored in the sketch: FritzingIvanBo?njak.ino
int trigPin = 11;
int echoPin = 12;
int A = 2;
int B = 3;
int C = 4;
int D = 5;
int E = 6;
int F = 7;
int G = 8;
int DP = 9;
long duration, cm, inches;


void setup() {
  Serial.begin (9600); 
  pinMode(trigPin, OUTPUT); 
  pinMode(echoPin, INPUT); 
  pinMode(A, OUTPUT); 
  pinMode(B, OUTPUT); 
  pinMode(C, OUTPUT); 
  pinMode(D, OUTPUT); 
  pinMode(E, OUTPUT); 
  pinMode(F, OUTPUT); 
  pinMode(G, OUTPUT); 
  pinMode(DP, OUTPUT); 
}
 
void loop() {
  digitalWrite(trigPin, LOW); 
  delayMicroseconds(5); 
  digitalWrite(trigPin, HIGH); 
  delayMicroseconds(10); 
  digitalWrite(trigPin, LOW); 
  pinMode(echoPin, INPUT); 


  duration = pulseIn(echoPin, HIGH);
  cm = (duration/2)/29.1;
  inches = (duration/2)/74; 


  Serial.print(inches); 
  Serial.print("in, ");
  Serial.print(cm); 
  Serial.print("cm");
  Serial.println();
  delay(250);


  if (cm < 20) {
    digitalWrite(A, LOW);
    digitalWrite(B, LOW);
    digitalWrite(C, LOW);
    digitalWrite(D, LOW);
    digitalWrite(E, LOW);
    digitalWrite(F, LOW);
    digitalWrite(G, LOW);
    digitalWrite(DP, LOW);
  }
  if (cm > 20) {
    digitalWrite(A, HIGH);
    digitalWrite(B, LOW);
    digitalWrite(C, HIGH);
    digitalWrite(D, HIGH);
    digitalWrite(E, HIGH);
    digitalWrite(F, LOW);
    digitalWrite(G, HIGH);
    digitalWrite(DP, HIGH);
  }
  if (cm > 40) {
    digitalWrite(A, HIGH);
    digitalWrite(B, HIGH);
    digitalWrite(C, LOW);
    digitalWrite(D, HIGH);
    digitalWrite(E, LOW);
    digitalWrite(F, HIGH);
    digitalWrite(G, HIGH);
    digitalWrite(DP, HIGH);
  }
  if (cm > 60) {
    digitalWrite(A, HIGH);
    digitalWrite(B, HIGH);
    digitalWrite(C, HIGH);
    digitalWrite(D, HIGH);
    digitalWrite(E, HIGH);
    digitalWrite(F, HIGH);
    digitalWrite(G, LOW);
    digitalWrite(DP, HIGH);
  }
}
