# Fritzing sketch sensor (saved by Fritzing 0.9.3b)
breadboards: 1

parts:
  Part1 = Arduino Uno (Rev3)
  hc-sr1 = hc-sr04
  U1 = 7-SEGMENT-DISPLAY [package=7-segment-display]
  R1 = Resistor [tolerance=±5% resistance=220 package="0603 [SMD]"]

nets:
  N1: Part1.D8, U1.E
  N2: Part1.D9_PWM, U1.B
  N3: Part1.D11_PWM/MOSI, hc-sr1.Trig
  N4: Part1.D12/MISO, hc-sr1.Echo
  N5: Part1.D2, U1.G2
  N6: Part1.D3_PWM, U1.A
  N7: Part1.D4, U1.DP
  N8: Part1.D5_PWM, U1.G1
  N9: Part1.D6_PWM, U1.D
  N10: Part1.D7, U1.G
  5V: Part1.5V, hc-sr1.VCC, R1.Pin_1
  GND: Part1.GND, hc-sr1.GND
  N11: U1.C, R1.Pin_0
